// Logisim project mupc.circ as structural Verilog
module main (
  input  in_1,
  input  in_2
);

  wire and_1_out, and_2_out, and_3_out, and_4_out, and_5_out, and_6_out, CLOCK_EXEC, CLOCK_FETCH,
       comparator_1_eq, comparator_2_eq, comparator_3_eq, comparator_4_eq, comparator_5_eq, comparator_6_eq,
       comparator_7_eq, comparator_8_gt, comparator_9_lt, d_ff_1_q, decoder_1_out0, decoder_1_out1,
       decoder_1_out2, decoder_1_out3, IMM_FLAG_INV, IS_JUMP, multiplexer_4_out, multiplexer_6_out,
       not_2_out, not_3_out, not_4_out;
  wire [1:0] REG_SELECT;
  wire [7:0] adder_2_out, adder_3_out, adder_4_out, adder_5_out, adder_6_out, and_7_out, bit_extender_1_out,
       bit_extender_2_out, IMMEDIATE, INSTRUCTION, multiplexer_7_out, multiplexer_8_out, multiplexer_9_out,
       multiplexer_10_out, multiplexer_11_out, or_2_out, ram_1_dout, random_1_out, REG_1, REG_2, REG_A,
       REG_B, REG_IN, shifter_1_out, subtractor_1_out, subtractor_2_out, xor_1_out;
  wire [15:0] adder_1_out, multiplexer_3_out, REG_ADDRESS, register_1_q;

  Clock clock_1 (.out(CLOCK_FETCH));
  not not_1 (CLOCK_EXEC, CLOCK_FETCH);
  Decoder #(.select(2)) decoder_1 (
    .out0(decoder_1_out0), .out1(decoder_1_out1), .out2(decoder_1_out2), .out3(decoder_1_out3),
    .sel(REG_SELECT), .en(IMM_FLAG_INV));
  Multiplexer #(.select(2), .width(8)) multiplexer_1 (
    .in0(REG_A), .in1(REG_B), .in2(REG_ADDRESS[15:8]), .in3(REG_ADDRESS[7:0]), .out(REG_1),
    .sel(INSTRUCTION[3:2]));
  Multiplexer #(.select(2), .width(8)) multiplexer_2 (
    .in0(REG_A), .in1(REG_B), .in2(REG_ADDRESS[15:8]), .in3(REG_ADDRESS[7:0]), .out(REG_2),
    .sel(INSTRUCTION[1:0]));
  Adder #(.width(16)) adder_1 (.a(register_1_q), .b(16'h1), .out(adder_1_out));  // open: cin, cout
  Multiplexer #(.width(16)) multiplexer_3 (
    .in0(adder_1_out), .in1(REG_ADDRESS), .out(multiplexer_3_out), .sel(IS_JUMP));
  Register #(.width(16)) register_1 (
    .D(multiplexer_3_out), .en(CLOCK_EXEC), .clk(CLOCK_EXEC), .Q(register_1_q), .clr(in_1));
  Register register_2 (.D(REG_IN), .en(decoder_1_out0), .clk(CLOCK_EXEC), .Q(REG_A), .clr(in_1));
  Register register_3 (.D(REG_IN), .en(decoder_1_out1), .clk(CLOCK_EXEC), .Q(REG_B), .clr(in_1));
  Register register_4 (.D(REG_IN), .en(decoder_1_out2), .clk(CLOCK_EXEC), .Q(REG_ADDRESS[15:8]), .clr(in_1));
  Register register_5 (.D(REG_IN), .en(decoder_1_out3), .clk(CLOCK_EXEC), .Q(REG_ADDRESS[7:0]), .clr(in_1));
  Multiplexer #(.select(4)) multiplexer_4 (
    .in0(1'b0), .in1(1'b0), .in2(1'b0), .in3(1'b0), .in4(1'b0), .in5(1'b0), .in6(1'b0), .in7(1'b1),
    .in8(1'b1), .in9(1'b0), .in10(1'b0), .in11(1'b0), .in12(1'b1), .in13(1'b1), .in14(1'b1), .in15(1'b1),
    .out(multiplexer_4_out), .sel(INSTRUCTION[7:4]));
  Comparator #(.width(4)) comparator_1 (.a(4'b1111), .b(INSTRUCTION[7:4]), .eq(comparator_1_eq));  // open: gt, lt
  RAM #(.addrWidth(16), .asyncread("true")) ram_1 (
    .addr(register_1_q), .oe(1'b1), .clk(CLOCK_EXEC), .dout(ram_1_dout));  // open: we, din
  Multiplexer #(.width(2)) multiplexer_5 (
    .in0(INSTRUCTION[3:2]), .in1(INSTRUCTION[1:0]), .out(REG_SELECT), .sel(multiplexer_4_out));
  not not_2 (not_2_out, d_ff_1_q);
  and and_1 (and_1_out, not_2_out, comparator_1_eq);
  D_Flip_Flop d_ff_1 (.D(and_1_out), .clk(CLOCK_FETCH), .Q(d_ff_1_q), .Qn(IMM_FLAG_INV), .reset(in_1));  // open: preset
  Comparator #(.width(4)) comparator_2 (.a(INSTRUCTION[7:4]), .b(4'b1000), .eq(comparator_2_eq));  // open: gt, lt
  Comparator #(.width(4)) comparator_3 (.a(INSTRUCTION[7:4]), .b(4'b1001), .eq(comparator_3_eq));  // open: gt, lt
  Comparator #(.width(4)) comparator_4 (.a(INSTRUCTION[7:4]), .b(4'b1010), .eq(comparator_4_eq));  // open: gt, lt
  Comparator #(.width(4)) comparator_5 (.a(INSTRUCTION[7:4]), .b(4'b1011), .eq(comparator_5_eq));  // open: gt, lt
  and and_2 (and_2_out, IMM_FLAG_INV, CLOCK_EXEC);
  not not_3 (not_3_out, comparator_6_eq);
  Comparator comparator_6 (.a(REG_2), .b({8{1'b0}}), .eq(comparator_6_eq));  // open: gt, lt
  not not_4 (not_4_out, and_2_out);
  Multiplexer #(.select(2)) multiplexer_6 (
    .in0(1'b1), .in1(comparator_6_eq), .in2(not_3_out), .in3(in_2), .out(multiplexer_6_out),
    .sel(INSTRUCTION[3:2]));
  Comparator comparator_7 (.a(REG_1), .b(REG_2), .eq(comparator_7_eq));  // open: gt, lt
  Comparator comparator_8 (.a(REG_1), .b(REG_2), .gt(comparator_8_gt));  // open: eq, lt
  Comparator comparator_9 (.a(REG_1), .b(REG_2), .lt(comparator_9_lt));  // open: gt, eq
  Register register_6 (.D(ram_1_dout), .en(and_2_out), .clk(and_2_out), .Q(INSTRUCTION), .clr(in_1));
  Register register_7 (.D(ram_1_dout), .en(not_4_out), .clk(not_4_out), .Q(IMMEDIATE), .clr(in_1));
  and and_3 (and_3_out, comparator_2_eq, multiplexer_6_out);
  and and_4 (and_4_out, comparator_3_eq, comparator_7_eq);
  and and_5 (and_5_out, comparator_4_eq, comparator_8_gt);
  and and_6 (and_6_out, comparator_5_eq, comparator_9_lt);
  or or_1 (IS_JUMP, and_3_out, and_4_out, and_5_out, and_6_out);
  assign bit_extender_1_out = {{7{1'b0}}, in_2};  // Bit_Extender bit_extender_1
  assign bit_extender_2_out = {{7{1'b0}}, in_2};  // Bit_Extender bit_extender_2
  Random random_1 (.clk(CLOCK_FETCH), .out(random_1_out));  // open: clr, next
  Adder adder_2 (.a(REG_2), .b(8'h1), .out(adder_2_out));  // open: cin, cout
  Subtractor subtractor_1 (.a(REG_2), .b(8'h1), .out(subtractor_1_out));  // open: bin, bout
  Adder adder_3 (.a(REG_2), .b(bit_extender_1_out), .out(adder_3_out));  // open: cin, cout
  Adder adder_4 (.a(REG_2), .b(bit_extender_2_out), .out(adder_4_out));  // open: cin, cout
  Adder adder_5 (.a(IMMEDIATE), .b(REG_2), .out(adder_5_out));  // open: cin, cout
  Adder adder_6 (.a(REG_1), .b(REG_2), .out(adder_6_out));  // open: cin, cout
  Subtractor subtractor_2 (.a(REG_1), .b(REG_2), .out(subtractor_2_out));  // open: bin, bout
  assign and_7_out = REG_1 & REG_2;  // AND_Gate and_7, 8 bits wide
  assign or_2_out = REG_1 | REG_2;  // OR_Gate or_2, 8 bits wide
  assign xor_1_out = REG_1 ^ REG_2;  // XOR_Gate xor_1, 8 bits wide
  Shifter #(.shift("lr")) shifter_1 (.in(REG_1), .\dist (REG_2[2:0]), .out(shifter_1_out));
  Multiplexer #(.select(2), .width(8)) multiplexer_7 (
    .in0(adder_2_out), .in1(subtractor_1_out), .in2(adder_3_out), .in3(adder_4_out), .out(multiplexer_7_out),
    .sel(INSTRUCTION[3:2]));
  Multiplexer #(.select(2), .width(8)) multiplexer_8 (
    .in0(REG_2), .in1(REG_2), .in2(REG_2), .in3(REG_2), .out(multiplexer_8_out), .sel(INSTRUCTION[3:2]));
  Multiplexer #(.select(2), .width(8)) multiplexer_9 (
    .in0(REG_2), .in1(REG_2), .out(multiplexer_9_out), .sel(INSTRUCTION[3:2]));  // open: in2, in3
  Multiplexer #(.select(2), .width(8)) multiplexer_10 (
    .in0(8'h1), .in1(random_1_out), .in2({8{1'b0}}), .in3({8{1'b0}}), .out(multiplexer_10_out),
    .sel(INSTRUCTION[3:2]));
  Multiplexer #(.select(2), .width(8)) multiplexer_11 (
    .in0(IMMEDIATE), .in1(adder_5_out), .out(multiplexer_11_out), .sel(INSTRUCTION[3:2]));  // open: in2, in3
  Multiplexer #(.select(4), .width(8)) multiplexer_12 (
    .in0(REG_2), .in1(adder_6_out), .in2(subtractor_2_out), .in3(and_7_out), .in4(or_2_out), .in5(xor_1_out),
    .in6(shifter_1_out), .in7(multiplexer_7_out), .in8(REG_2), .in9(REG_1), .in10(REG_1), .in11(REG_1),
    .in12(multiplexer_8_out), .in13(multiplexer_9_out), .in14(multiplexer_10_out), .in15(multiplexer_11_out),
    .out(REG_IN), .sel(INSTRUCTION[7:4]));

  // Other names for the same wires on the sheet: CARRY = in_2; R2_SEL[1:0] = INSTRUCTION[1:0];
  //   REG_D[7:0] = REG_ADDRESS[7:0]; REG_C[7:0] = REG_ADDRESS[15:8]; RESET = in_1; R1_SEL[1:0] = INSTRUCTION[3:2];
  //   SUB_OP[5:0] = INSTRUCTION[7:2]; OPCODE[3:0] = INSTRUCTION[7:4]

  // Notes on the sheet:
  //   TODO read mem
  //   TODO read io
  //   Simple jumps
  //   TODO pop
  //   JE
  //   JG
  //   JL
endmodule
